# Fritzing sketch setup (saved by Fritzing 0.9.5d)
breadboards: 1

parts:
  WeMos_D1_Mini1 = WeMos D1 Mini
  Part1 = GY-VL53L0XV2 Laser Ranger Module
  Part2 = GY-VL53L0XV2 Laser Ranger Module
  LED2 = LED - 5mm [color="Red (633nm)" package="5 mm [THT]"]
  LED3 = LED - 5mm [color="Yellow (595nm)" package="5 mm [THT]"]
  LED4 = LED - 5mm [color="Green (570nm)" package="5 mm [THT]"]
  R1 = Resistor [tolerance=±5% resistance=330 package=THT]
  R2 = Resistor [tolerance=±5% resistance=330 package=THT]
  R3 = Resistor [tolerance=±5% resistance=330 package="2512 [SMD]"]
  R3_2 = Resistor [tolerance=±5% resistance=330 package=THT]

nets:
  VCC: WeMos_D1_Mini1.5V, Part1.VCC, Part2.VCC
  N1: WeMos_D1_Mini1.D1, Part1.SCL, Part2.SCL
  N2: WeMos_D1_Mini1.D2, Part1.SDA
  N3: WeMos_D1_Mini1.D4, WeMos_D1_Mini1.D7, WeMos_D1_Mini1.D8, LED2.anode, LED3.anode, LED4.anode
  N4: WeMos_D1_Mini1.D5, Part1.XSHUT
  N5: WeMos_D1_Mini1.D6, Part2.XSHUT
  GND: WeMos_D1_Mini1.G, Part1.GND, Part2.GND, R1.Pin_1, R2.Pin_1, R3.Pin_1, R3_2.Pin_1
  N6: LED2.cathode, R1.Pin_0
  N7: LED3.cathode, R2.Pin_0
  N8: LED4.cathode, R3.Pin_0, R3_2.Pin_0

notes:
  entry sensor
  exit sensor

custom parts:
  GY-VL53L0XV2 Laser Ranger Module: The GY-VL53L0XV2 is based on the VL53L0X from ST Microelectronics, a time-of-flight ranging system integrated into a compact module.
